// Logisim project ADDER .circ as structural Verilog: 1 circuit, main circuit main
module main (
  input  C,
  input  [1:0] in_2,
  input  [1:0] s1s0,
  input  a3,
  input  a2,
  input  a1,
  input  a0,
  input  b0,
  input  b1,
  input  b2,
  input  b3,
  output out_12,
  output q0,
  output out_14,
  output carry
);

  wire and_15_out, multiplexer_4_out, multiplexer_5_out, multiplexer_10_out, multiplexer_11_out,
       multiplexer_14_out, multiplexer_17_out, multiplexer_19_out, multiplexer_20_out, multiplexer_22_out,
       multiplexer_23_out, multiplexer_24_out, multiplexer_25_out, multiplexer_26_out, multiplexer_27_out,
       multiplexer_28_out, not_1_out, not_2_out, not_3_out, not_4_out, not_5_out, not_6_out, not_7_out,
       not_8_out, not_9_out;
  wire [1:0] and_3_out, and_4_out, and_5_out, and_6_out, and_7_out, and_10_out, and_11_out, and_12_out,
       and_13_out, and_14_out, and_16_out, multiplexer_9_out;

  and and_1 (multiplexer_9_out[1], b1, a3);
  not not_1 (not_1_out, C);
  and and_2 (and_5_out[1], b0, a3);
  Multiplexer #(.select(2), .enable("false")) multiplexer_1 (
    .in0(1'b0), .in1(1'b0), .in2(1'b0), .in3(1'b1), .out(and_3_out[1]), .sel(multiplexer_9_out));
  Multiplexer #(.select(2), .enable("false")) multiplexer_2 (
    .in0(1'b0), .in1(1'b1), .in2(1'b1), .in3(1'b0), .out(and_6_out[1]), .sel(multiplexer_9_out));
  and and_3 (and_3_out[0], b2, a3);
  Multiplexer #(.select(2), .enable("false")) multiplexer_3 (
    .in0(1'b0), .in1(multiplexer_10_out), .in2(multiplexer_10_out), .in3(1'b1), .out(and_4_out[1]),
    .sel(and_3_out));
  and and_4 (and_4_out[0], b3, a3);
  not not_2 (not_2_out, multiplexer_11_out);
  Multiplexer #(.select(2), .enable("false")) multiplexer_4 (
    .in0(multiplexer_11_out), .in1(not_2_out), .in2(not_2_out), .in3(multiplexer_11_out),
    .out(multiplexer_4_out), .sel(and_4_out));
  Multiplexer #(.select(2), .enable("false")) multiplexer_5 (
    .in0(1'b0), .in1(multiplexer_11_out), .in2(multiplexer_11_out), .in3(1'b1), .out(multiplexer_5_out),
    .sel(and_4_out));
  Multiplexer #(.select(2), .enable("false")) multiplexer_6 (
    .in0(C), .in1(not_1_out), .in2(not_1_out), .in3(C), .out(q0), .sel(s1s0));
  Multiplexer #(.select(2), .enable("false")) multiplexer_7 (
    .in0(1'b0), .in1(C), .in2(C), .in3(1'b1), .out(carry), .sel(s1s0));
  not not_3 (not_3_out, multiplexer_10_out);
  Multiplexer #(.select(2), .enable("false")) multiplexer_8 (
    .in0(multiplexer_10_out), .in1(not_3_out), .in2(not_3_out), .in3(multiplexer_10_out), .out(and_7_out[1]),
    .sel(and_3_out));
  and and_5 (and_5_out[0], b1, a2);
  Multiplexer #(.select(2), .enable("false")) multiplexer_9 (
    .in0(1'b0), .in1(multiplexer_19_out), .in2(multiplexer_19_out), .in3(1'b1), .out(multiplexer_9_out[0]),
    .sel(and_5_out));
  and and_6 (and_6_out[0], b2, a2);
  Multiplexer #(.select(2), .enable("false")) multiplexer_10 (
    .in0(1'b0), .in1(multiplexer_20_out), .in2(multiplexer_20_out), .in3(1'b1), .out(multiplexer_10_out),
    .sel(and_6_out));
  and and_7 (and_7_out[0], b3, a2);
  Multiplexer #(.select(2), .enable("false")) multiplexer_11 (
    .in0(1'b0), .in1(multiplexer_17_out), .in2(multiplexer_17_out), .in3(1'b1), .out(multiplexer_11_out),
    .sel(and_7_out));
  and and_8 (and_10_out[1], b0, a2);
  not not_4 (not_4_out, multiplexer_19_out);
  Multiplexer #(.select(2), .enable("false")) multiplexer_12 (
    .in0(multiplexer_19_out), .in1(not_4_out), .in2(not_4_out), .in3(multiplexer_19_out),
    .out(and_11_out[1]), .sel(and_5_out));
  not not_5 (not_5_out, multiplexer_20_out);
  Multiplexer #(.select(2), .enable("false")) multiplexer_13 (
    .in0(multiplexer_20_out), .in1(not_5_out), .in2(not_5_out), .in3(multiplexer_20_out),
    .out(and_12_out[1]), .sel(and_6_out));
  not not_6 (not_6_out, multiplexer_17_out);
  Multiplexer #(.select(2), .enable("false")) multiplexer_14 (
    .in0(multiplexer_17_out), .in1(not_6_out), .in2(not_6_out), .in3(multiplexer_17_out),
    .out(multiplexer_14_out), .sel(and_7_out));
  Multiplexer #(.select(2), .enable("false")) multiplexer_15 (
    .in0(1'b0), .in1(1'b1), .in2(1'b1), .in3(1'b0), .out(out_12), .sel(in_2));
  Multiplexer #(.select(2), .enable("false")) multiplexer_16 (
    .in0(1'b0), .in1(1'b0), .in2(1'b0), .in3(1'b1), .out(out_14), .sel(in_2));
  Multiplexer #(.select(2), .enable("false")) multiplexer_17 (
    .in0(1'b0), .in1(multiplexer_24_out), .in2(multiplexer_24_out), .in3(1'b1), .out(multiplexer_17_out),
    .sel(and_12_out));
  and and_9 (and_16_out[1], b0, a1);
  and and_10 (and_10_out[0], b1, a1);
  not not_7 (not_7_out, multiplexer_25_out);
  Multiplexer #(.select(2), .enable("false")) multiplexer_18 (
    .in0(multiplexer_25_out), .in1(not_7_out), .in2(not_7_out), .in3(multiplexer_25_out),
    .out(and_13_out[1]), .sel(and_10_out));
  Multiplexer #(.select(2), .enable("false")) multiplexer_19 (
    .in0(1'b0), .in1(multiplexer_25_out), .in2(multiplexer_25_out), .in3(1'b1), .out(multiplexer_19_out),
    .sel(and_10_out));
  and and_11 (and_11_out[0], b2, a1);
  not not_8 (not_8_out, multiplexer_23_out);
  Multiplexer #(.select(2), .enable("false")) multiplexer_20 (
    .in0(1'b0), .in1(multiplexer_23_out), .in2(multiplexer_23_out), .in3(1'b1), .out(multiplexer_20_out),
    .sel(and_11_out));
  Multiplexer #(.select(2), .enable("false")) multiplexer_21 (
    .in0(multiplexer_23_out), .in1(not_8_out), .in2(not_8_out), .in3(multiplexer_23_out),
    .out(and_14_out[1]), .sel(and_11_out));
  and and_12 (and_12_out[0], b3, a1);
  not not_9 (not_9_out, multiplexer_24_out);
  Multiplexer #(.select(2), .enable("false")) multiplexer_22 (
    .in0(multiplexer_24_out), .in1(not_9_out), .in2(not_9_out), .in3(multiplexer_24_out),
    .out(multiplexer_22_out), .sel(and_12_out));
  Multiplexer #(.select(2), .enable("false")) multiplexer_23 (
    .in0(1'b0), .in1(1'b0), .in2(1'b0), .in3(1'b1), .out(multiplexer_23_out), .sel(and_13_out));
  Multiplexer #(.select(2), .enable("false")) multiplexer_24 (
    .in0(1'b0), .in1(1'b0), .in2(1'b0), .in3(1'b1), .out(multiplexer_24_out), .sel(and_14_out));
  Multiplexer #(.select(2), .enable("false")) multiplexer_25 (
    .in0(1'b0), .in1(1'b0), .in2(1'b0), .in3(1'b1), .out(multiplexer_25_out), .sel(and_16_out));
  and and_13 (and_13_out[0], b2, a0);
  Multiplexer #(.select(2), .enable("false")) multiplexer_26 (
    .in0(1'b0), .in1(1'b1), .in2(1'b1), .in3(1'b0), .out(multiplexer_26_out), .sel(and_13_out));
  and and_14 (and_14_out[0], b3, a0);
  Multiplexer #(.select(2), .enable("false")) multiplexer_27 (
    .in0(1'b0), .in1(1'b1), .in2(1'b1), .in3(1'b0), .out(multiplexer_27_out), .sel(and_14_out));
  and and_15 (and_15_out, b0, a0);
  and and_16 (and_16_out[0], b1, a0);
  Multiplexer #(.select(2), .enable("false")) multiplexer_28 (
    .in0(1'b0), .in1(1'b1), .in2(1'b1), .in3(1'b0), .out(multiplexer_28_out), .sel(and_16_out));

  // Notes on the sheet:
  //   z7
  //   FULL ADDER
  //   z6
  //   sum
  //   q1
  //   z5
  //   HALF ADDER
  //   z4
  //   z2
  //   z3
  //   z1
  //   z0
endmodule
